// Logisim project afsgsLGsdg.circ as structural Verilog: 1 circuit, main circuit main
module main (
  input  M1,
  input  M2,
  input  \Butão ,
  output \Doseador_Café ,
  output Bomba_de_Agua,
  output \Doseador_de_Açucar 
);

  wire and_1_out, and_2_out, and_3_out, and_4_out, and_5_out, and_6_out, and_7_out, and_8_out, and_9_out,
       and_10_out, and_11_out, and_12_out, and_13_out, and_14_out, and_15_out, and_16_out, and_17_out,
       and_18_out, and_21_out, and_22_out, clock_1_out, not_1_out, not_2_out, not_3_out, or_1_out, or_2_out,
       or_3_out, or_4_out, or_5_out, or_6_out, or_7_out, x0_2_q, x0_2_qn, x0_q, x0_qn, x1_2_qn, x1_q, x1_qn,
       x2_q, x2_qn;

  and and_1 (and_1_out, \Butão , and_18_out);
  Clock clock_1 (.out(clock_1_out));
  not not_1 (not_1_out, M1);
  not not_2 (not_2_out, M2);
  not not_3 (not_3_out, and_21_out);
  and and_2 (and_2_out, x2_q, x1_2_qn, x0_2_qn);
  or or_1 (or_1_out, and_2_out, and_3_out);
  and and_3 (and_3_out, x2_qn, Bomba_de_Agua, x0_2_q);
  and and_4 (and_4_out, not_1_out, M2, x1_qn);
  and and_5 (and_5_out, M1, not_2_out, x1_qn, x0_q);
  and and_6 (and_6_out, x1_q, x0_qn);
  and and_7 (and_7_out, not_3_out, x1_q);
  D_Flip_Flop x2 (.clk(clock_1_out), .D(or_1_out), .Q(x2_q), .Qn(x2_qn));  // open: preset, en, reset
  or or_2 (or_2_out, and_4_out, and_5_out, and_6_out, and_7_out);
  D_Flip_Flop x1 (.clk(clock_1_out), .D(or_2_out), .Q(x1_q), .Qn(x1_qn));  // open: preset, en, reset
  and and_8 (and_8_out, x2_qn, x1_2_qn, x0_2_q);
  or or_3 (or_3_out, and_8_out, and_9_out);
  and and_9 (and_9_out, x2_qn, Bomba_de_Agua, x0_2_qn);
  D_Flip_Flop x1_2 (.clk(clock_1_out), .D(or_3_out), .Q(Bomba_de_Agua), .Qn(x1_2_qn));  // open: preset, en, reset
  and and_10 (and_10_out, M1, not_2_out, x0_qn);
  and and_11 (and_11_out, not_1_out, x1_qn, x0_q);
  and and_12 (and_12_out, M2, x1_qn, x0_q);
  and and_13 (and_13_out, not_1_out, M2, x1_q, x0_qn);
  and and_14 (and_14_out, not_3_out, x1_q, x0_q);
  and and_15 (and_15_out, x2_q, x1_2_qn, x0_2_qn);
  and and_16 (and_16_out, x2_qn, Bomba_de_Agua, x0_2_qn);
  and and_17 (and_17_out, x2_qn, x0_2_qn, and_1_out);
  or or_4 (or_4_out, and_15_out, and_16_out, and_17_out);
  D_Flip_Flop x0 (.clk(clock_1_out), .D(or_5_out), .Q(x0_q), .Qn(x0_qn));  // open: preset, en, reset
  or or_5 (or_5_out, and_10_out, and_11_out, and_12_out, and_13_out, and_14_out);
  D_Flip_Flop x0_2 (.clk(clock_1_out), .D(or_4_out), .Q(x0_2_q), .Qn(x0_2_qn));  // open: preset, en, reset
  and and_18 (and_18_out, x0_q, x1_q);
  and and_19 (\Doseador_Café , x2_qn, x1_2_qn, x0_2_q);
  and and_20 (\Doseador_de_Açucar , x2_q, x1_2_qn, x0_2_qn);
  and and_21 (and_21_out, x2_q, x1_2_qn, x0_2_q);
  or or_6 (or_6_out, x1_q, x0_qn);
  or or_7 (or_7_out, x0_q, x1_qn);
  and and_22 (and_22_out, x1_qn, x0_qn);
  LED \Café_Pronto  (.in(and_21_out));
  _7_Segment_Display u_7_segment_display_1 (
    .g(x1_q), .f(and_22_out), .a(or_6_out), .b(1'b1), .e(x0_qn), .d(or_6_out), .c(or_7_out));  // open: dp
  LED \Tirar_Café  (.in(and_18_out));
endmodule
